# Fritzing sketch Rasp_launcher (saved by Fritzing 0.8.7b)
breadboards: 2

parts:
  M2 = Stepper Motor - Unipolar
  J2 = Basic Servo
  Raspberry_Pi_B_rev2 = Raspberry Pi B rev2  # not connected
  IC1 = ULN2003A [package="DIP16 [THT]"]
  Componente1 = Arduino Nano (Rev3.0)

nets:
  N1: M2.A, IC1.Out_1
  VCC: M2.COMMON_1, J2.vcc, Componente1.5V
  N2: M2.C, IC1.Out_3
  N3: M2.B, IC1.Out_2
  N4: M2.COMMON_2, IC1.Out_4
  GND: M2.D, J2.gnd, Componente1.GND

notes:
  Rasp Launcher:
  Desenvolvido no Hackaton do @soujava na Campus Party 2014.
